# Fritzing sketch RP2040-OLED-Tester (saved by Fritzing 1.0.5)
breadboards: 1

parts:
  OLED1 = OLED 128x64 I2C Monochrome Display GND-VDD
  A1 = Waveshare rp2040-zero smd [package=SMD]
  S1 = Momentary Switch 6mm 2pin  # not connected
  S2 = Momentary Switch 6mm 2pin

nets:
  N1: OLED1.GND, A1.Pin_2, A1.Pin_33, S2.2
  N2: OLED1.VDD, A1.Pin_3
  N3: OLED1.SCK, A1.Pin_18
  N4: OLED1.SDA, A1.Pin_19

notes:
  RP2040-Zero
  ブレッドボード 170H
  OLED モジュール
  タクトスイッチ x2

custom parts:
  OLED 128x64 I2C Monochrome Display GND-VDD: OLED 128x64 I2C Monochrome Display. Note: there are two variants of this part, this one is the GND VDD SCK SDA variant. The other is VDD GND SCK SDA. Make sure you select the part that matches your module as using the incorrect part will probably destroy your module! In addition the mounting holes are marked on silkscreen but not by default drilled. If you want drilled mounting holes, copy a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
  Waveshare rp2040-zero smd: .RP2040-Zero, A Low-Cost, High-Performance Pico-Like MCU Board Based On Raspberry Pi Microcontroller RP2040. This varant is SMD with all the connections.
  Momentary Switch 6mm 2pin: Momentary Switch 6mm 2 pin Button commonly used for reset or general input.
